// Logisim project DLD.circ as structural Verilog: 1 circuit, main circuit main
module main (
  input  in_1,
  input  in_2,
  input  in_3,
  input  in_4,
  input  in_5,
  input  in_6,
  input  in_7,
  input  in_8,
  input  in_9
);

  wire and_1_out, and_2_out, and_3_out, and_4_out, nand_1_out, not_1_out, xnor_1_out, xnor_2_out, xnor_3_out,
       xnor_4_out;

  xnor xnor_1 (xnor_1_out, in_1, in_5);
  xnor xnor_2 (xnor_2_out, in_2, in_6);
  xnor xnor_3 (xnor_3_out, in_3, in_8);
  xnor xnor_4 (xnor_4_out, in_4, in_9);
  and and_1 (and_1_out, xnor_1_out, xnor_2_out);
  and and_2 (and_2_out, xnor_3_out, xnor_4_out);
  nand nand_1 (nand_1_out, and_1_out, and_2_out);
  not not_1 (not_1_out, nand_1_out);
  and and_3 (and_3_out, not_1_out, in_7);
  and and_4 (and_4_out, nand_1_out, in_7, in_7);
  LED led_1 (.in(and_3_out));
  LED led_2 (.in(and_4_out));
endmodule
