// Logisim project dlddiff.circ as structural Verilog: 1 circuit, main circuit main
module main (
  input  in_1,
  input  in_2,
  input  in_3,
  input  in_4,
  input  in_5,
  input  in_6,
  input  in_7,
  input  in_8,
  input  in_9,
  output out_10,
  output out_11,
  output out_12,
  output out_13
);

  wire and_1_out, and_2_out, clock_1_out, j_k_ff_1_q, j_k_ff_1_qn, j_k_ff_2_q, j_k_ff_2_qn, j_k_ff_3_q,
       j_k_ff_3_qn, nand_1_out, not_1_out, not_2_out, not_3_out, xnor_1_out, xnor_2_out, xnor_3_out,
       xnor_4_out;

  xnor xnor_1 (xnor_1_out, in_1, in_5);
  xnor xnor_2 (xnor_2_out, in_2, in_6);
  xnor xnor_3 (xnor_3_out, in_3, in_7);
  xnor xnor_4 (xnor_4_out, in_4, in_8);
  not not_1 (not_1_out, out_10);
  Clock clock_1 (.out(clock_1_out));
  J_K_Flip_Flop j_k_ff_1 (
    .J(out_10), .clk(clock_1_out), .K(not_1_out), .Q(j_k_ff_1_q), .Qn(j_k_ff_1_qn));  // open: preset, en, reset
  and and_1 (and_1_out, xnor_1_out, xnor_2_out);
  and and_2 (and_2_out, xnor_3_out, xnor_4_out);
  J_K_Flip_Flop j_k_ff_2 (
    .J(j_k_ff_1_q), .clk(clock_1_out), .K(j_k_ff_1_qn), .Q(j_k_ff_2_q), .Qn(j_k_ff_2_qn));  // open: preset, en, reset
  nand nand_1 (nand_1_out, and_1_out, and_2_out);
  J_K_Flip_Flop j_k_ff_3 (
    .J(j_k_ff_2_q), .clk(clock_1_out), .K(j_k_ff_2_qn), .Q(j_k_ff_3_q), .Qn(j_k_ff_3_qn));  // open: preset, en, reset
  not not_2 (not_2_out, nand_1_out);
  J_K_Flip_Flop j_k_ff_4 (
    .J(j_k_ff_3_q), .clk(clock_1_out), .K(j_k_ff_3_qn), .Q(out_12));  // open: Qn, preset, en, reset
  and and_3 (out_10, not_2_out, in_9);
  and and_4 (out_11, nand_1_out, in_9, in_9);
  not not_3 (not_3_out, out_11);
  and and_5 (out_13, out_10, out_12, not_3_out, in_9);
  LED led_1 (.in(out_13));
endmodule
