// Logisim project dlddifflong.circ as structural Verilog: 1 circuit, main circuit main
module main (
  input  a,
  input  b,
  input  c,
  input  d,
  input  e,
  input  f,
  input  g,
  input  h,
  input  x2,
  output x,
  output y,
  output z,
  output u
);

  wire and_1_out, and_2_out, and_3_out, and_4_out, and_5_out, and_6_out, and_7_out, and_8_out, and_9_out,
       and_10_out, and_11_out, and_12_out, and_13_out, and_14_out, and_15_out, and_16_out, and_17_out,
       and_18_out, and_19_out, and_20_out, and_21_out, and_22_out, and_23_out, and_24_out, and_25_out,
       and_26_out, and_27_out, and_28_out, and_29_out, and_30_out, and_31_out, and_32_out, and_33_out,
       and_34_out, and_35_out, and_36_out, and_37_out, and_38_out, and_39_out, and_40_out, and_41_out,
       and_42_out, and_43_out, and_44_out, and_45_out, and_46_out, and_47_out, and_48_out, and_49_out,
       and_50_out, and_51_out, and_52_out, and_53_out, and_54_out, and_55_out, and_56_out, not_1_out,
       not_2_out, not_3_out, not_4_out, not_5_out, not_6_out, not_7_out, not_8_out, not_9_out, not_10_out,
       not_11_out, not_12_out, not_13_out, not_14_out, not_15_out, not_16_out, not_17_out, not_18_out,
       not_19_out, not_20_out, not_21_out, not_22_out, not_23_out, not_24_out, not_25_out, not_26_out,
       not_27_out, not_28_out, not_29_out, not_30_out, not_31_out, not_32_out, not_33_out, not_34_out,
       not_35_out, not_36_out, not_37_out, not_38_out, not_39_out, not_40_out, not_41_out, not_42_out,
       not_43_out, not_44_out, not_45_out, not_46_out, not_47_out, not_48_out, not_49_out, not_50_out,
       not_51_out, not_52_out, not_53_out, not_54_out, not_55_out, not_56_out, not_57_out, not_58_out,
       not_59_out, not_60_out, not_61_out, not_62_out, not_63_out, not_64_out, not_65_out, not_66_out,
       not_67_out, not_68_out, not_69_out, not_70_out, not_71_out, not_72_out, not_73_out, not_74_out,
       not_75_out, not_76_out, not_77_out, not_78_out, not_79_out, not_80_out, not_81_out, not_82_out,
       not_83_out, not_84_out, not_85_out, not_86_out, not_87_out, not_88_out, not_89_out, not_90_out,
       not_91_out, not_92_out, not_93_out, not_94_out, not_95_out, not_96_out, not_97_out, not_98_out,
       not_99_out, not_100_out, not_101_out, not_102_out, not_103_out, not_104_out, not_105_out, not_106_out,
       not_107_out, not_108_out, not_109_out, not_110_out, not_111_out, not_112_out, not_113_out,
       not_114_out, not_115_out, not_116_out, not_117_out, not_118_out, not_119_out, not_120_out,
       not_121_out, not_122_out, not_123_out, not_124_out, not_125_out, not_126_out, not_127_out,
       not_128_out, not_129_out, not_130_out, not_131_out, not_132_out, not_133_out, not_134_out,
       not_135_out, not_136_out, not_137_out, not_138_out, not_139_out, not_140_out, not_141_out,
       not_142_out, not_143_out, not_144_out, not_145_out, not_146_out, not_147_out, not_148_out,
       not_149_out, not_150_out, not_151_out, not_152_out, not_153_out, not_154_out, not_155_out,
       not_156_out, not_157_out, not_158_out, not_159_out, not_160_out, not_161_out, not_162_out,
       not_163_out, not_164_out, not_165_out, not_166_out, not_167_out, not_168_out, not_169_out,
       not_170_out, not_171_out, not_172_out, not_173_out, not_174_out, not_175_out, not_176_out,
       not_177_out, not_178_out, not_179_out, not_180_out, not_181_out, not_182_out, not_183_out,
       not_184_out, not_185_out, not_186_out, not_187_out, not_188_out, not_189_out, not_190_out,
       not_191_out, not_192_out, not_193_out, not_194_out, not_195_out, not_196_out, not_197_out,
       not_198_out, not_199_out, not_200_out;

  not not_1 (not_1_out, a);
  not not_2 (not_2_out, b);
  not not_3 (not_3_out, c);
  not not_4 (not_4_out, d);
  not not_5 (not_5_out, e);
  not not_6 (not_6_out, f);
  not not_7 (not_7_out, g);
  not not_8 (not_8_out, h);
  not not_9 (not_9_out, a);
  not not_10 (not_10_out, b);
  not not_11 (not_11_out, c);
  not not_12 (not_12_out, e);
  not not_13 (not_13_out, f);
  not not_14 (not_14_out, g);
  not not_15 (not_15_out, a);
  not not_16 (not_16_out, b);
  not not_17 (not_17_out, d);
  not not_18 (not_18_out, e);
  not not_19 (not_19_out, f);
  not not_20 (not_20_out, h);
  not not_21 (not_21_out, a);
  not not_22 (not_22_out, b);
  not not_23 (not_23_out, e);
  not not_24 (not_24_out, f);
  not not_25 (not_25_out, a);
  not not_26 (not_26_out, c);
  not not_27 (not_27_out, d);
  not not_28 (not_28_out, e);
  not not_29 (not_29_out, g);
  not not_30 (not_30_out, h);
  not not_31 (not_31_out, a);
  not not_32 (not_32_out, c);
  not not_33 (not_33_out, e);
  not not_34 (not_34_out, g);
  not not_35 (not_35_out, a);
  not not_36 (not_36_out, d);
  not not_37 (not_37_out, e);
  not not_38 (not_38_out, h);
  not not_39 (not_39_out, a);
  not not_40 (not_40_out, e);
  not not_41 (not_41_out, b);
  not not_42 (not_42_out, c);
  not not_43 (not_43_out, d);
  not not_44 (not_44_out, f);
  not not_45 (not_45_out, g);
  not not_46 (not_46_out, h);
  not not_47 (not_47_out, b);
  not not_48 (not_48_out, c);
  not not_49 (not_49_out, f);
  not not_50 (not_50_out, g);
  not not_51 (not_51_out, b);
  not not_52 (not_52_out, d);
  not not_53 (not_53_out, f);
  not not_54 (not_54_out, h);
  not not_55 (not_55_out, b);
  not not_56 (not_56_out, f);
  not not_57 (not_57_out, c);
  not not_58 (not_58_out, d);
  not not_59 (not_59_out, g);
  not not_60 (not_60_out, h);
  not not_61 (not_61_out, c);
  not not_62 (not_62_out, g);
  not not_63 (not_63_out, d);
  not not_64 (not_64_out, h);
  not not_65 (not_65_out, d);
  not not_66 (not_66_out, c);
  not not_67 (not_67_out, b);
  not not_68 (not_68_out, a);
  not not_69 (not_69_out, h);
  not not_70 (not_70_out, g);
  not not_71 (not_71_out, f);
  not not_72 (not_72_out, e);
  not not_73 (not_73_out, a);
  not not_74 (not_74_out, b);
  not not_75 (not_75_out, c);
  not not_76 (not_76_out, d);
  not not_77 (not_77_out, e);
  not not_78 (not_78_out, f);
  not not_79 (not_79_out, g);
  not not_80 (not_80_out, h);
  not not_81 (not_81_out, a);
  not not_82 (not_82_out, b);
  not not_83 (not_83_out, c);
  not not_84 (not_84_out, e);
  not not_85 (not_85_out, f);
  not not_86 (not_86_out, g);
  not not_87 (not_87_out, a);
  not not_88 (not_88_out, b);
  not not_89 (not_89_out, d);
  not not_90 (not_90_out, e);
  not not_91 (not_91_out, f);
  not not_92 (not_92_out, h);
  not not_93 (not_93_out, a);
  not not_94 (not_94_out, b);
  not not_95 (not_95_out, e);
  not not_96 (not_96_out, f);
  not not_97 (not_97_out, a);
  not not_98 (not_98_out, c);
  not not_99 (not_99_out, d);
  not not_100 (not_100_out, e);
  not not_101 (not_101_out, g);
  not not_102 (not_102_out, h);
  not not_103 (not_103_out, a);
  not not_104 (not_104_out, c);
  not not_105 (not_105_out, e);
  not not_106 (not_106_out, g);
  not not_107 (not_107_out, a);
  not not_108 (not_108_out, d);
  not not_109 (not_109_out, e);
  not not_110 (not_110_out, h);
  not not_111 (not_111_out, a);
  not not_112 (not_112_out, e);
  not not_113 (not_113_out, b);
  not not_114 (not_114_out, c);
  not not_115 (not_115_out, d);
  not not_116 (not_116_out, f);
  not not_117 (not_117_out, g);
  not not_118 (not_118_out, h);
  not not_119 (not_119_out, b);
  not not_120 (not_120_out, c);
  not not_121 (not_121_out, f);
  not not_122 (not_122_out, g);
  not not_123 (not_123_out, b);
  not not_124 (not_124_out, d);
  not not_125 (not_125_out, f);
  not not_126 (not_126_out, h);
  not not_127 (not_127_out, b);
  not not_128 (not_128_out, f);
  not not_129 (not_129_out, c);
  not not_130 (not_130_out, d);
  not not_131 (not_131_out, g);
  not not_132 (not_132_out, h);
  not not_133 (not_133_out, c);
  not not_134 (not_134_out, g);
  not not_135 (not_135_out, d);
  not not_136 (not_136_out, h);
  not not_137 (not_137_out, a);
  not not_138 (not_138_out, b);
  not not_139 (not_139_out, c);
  not not_140 (not_140_out, d);
  not not_141 (not_141_out, e);
  not not_142 (not_142_out, f);
  not not_143 (not_143_out, g);
  not not_144 (not_144_out, h);
  not not_145 (not_145_out, a);
  not not_146 (not_146_out, b);
  not not_147 (not_147_out, c);
  not not_148 (not_148_out, e);
  not not_149 (not_149_out, f);
  not not_150 (not_150_out, g);
  not not_151 (not_151_out, a);
  not not_152 (not_152_out, b);
  not not_153 (not_153_out, d);
  not not_154 (not_154_out, e);
  not not_155 (not_155_out, f);
  not not_156 (not_156_out, h);
  not not_157 (not_157_out, a);
  not not_158 (not_158_out, b);
  not not_159 (not_159_out, e);
  not not_160 (not_160_out, f);
  not not_161 (not_161_out, a);
  not not_162 (not_162_out, c);
  not not_163 (not_163_out, d);
  not not_164 (not_164_out, e);
  not not_165 (not_165_out, g);
  not not_166 (not_166_out, h);
  not not_167 (not_167_out, a);
  not not_168 (not_168_out, c);
  not not_169 (not_169_out, e);
  not not_170 (not_170_out, g);
  not not_171 (not_171_out, a);
  not not_172 (not_172_out, d);
  not not_173 (not_173_out, e);
  not not_174 (not_174_out, h);
  not not_175 (not_175_out, a);
  not not_176 (not_176_out, e);
  not not_177 (not_177_out, b);
  not not_178 (not_178_out, c);
  not not_179 (not_179_out, d);
  not not_180 (not_180_out, f);
  not not_181 (not_181_out, g);
  not not_182 (not_182_out, h);
  not not_183 (not_183_out, b);
  not not_184 (not_184_out, c);
  not not_185 (not_185_out, f);
  not not_186 (not_186_out, g);
  not not_187 (not_187_out, b);
  not not_188 (not_188_out, d);
  not not_189 (not_189_out, f);
  not not_190 (not_190_out, h);
  not not_191 (not_191_out, b);
  not not_192 (not_192_out, f);
  not not_193 (not_193_out, c);
  not not_194 (not_194_out, d);
  not not_195 (not_195_out, g);
  not not_196 (not_196_out, h);
  not not_197 (not_197_out, c);
  not not_198 (not_198_out, g);
  not not_199 (not_199_out, d);
  not not_200 (not_200_out, h);
  and and_1 (and_1_out, not_1_out, not_2_out, not_3_out, not_4_out, not_5_out, not_6_out, not_7_out, not_8_out, x2);
  and and_2 (and_2_out, not_9_out, not_10_out, not_11_out, d, not_12_out, not_13_out, not_14_out, h, x2);
  and and_3 (and_3_out, not_15_out, not_16_out, c, not_17_out, not_18_out, not_19_out, g, not_20_out, x2);
  and and_4 (and_4_out, not_21_out, not_22_out, c, d, not_23_out, not_24_out, g, h, x2);
  and and_5 (and_5_out, not_25_out, b, not_26_out, not_27_out, not_28_out, f, not_29_out, not_30_out, x2);
  and and_6 (and_6_out, not_31_out, b, not_32_out, d, not_33_out, f, not_34_out, h, x2);
  and and_7 (and_7_out, not_35_out, b, c, not_36_out, not_37_out, f, g, not_38_out, x2);
  and and_8 (and_8_out, not_39_out, b, c, d, not_40_out, f, g, h, x2);
  and and_9 (and_9_out, a, not_41_out, not_42_out, not_43_out, e, not_44_out, not_45_out, not_46_out, x2);
  and and_10 (and_10_out, a, not_47_out, not_48_out, d, e, not_49_out, not_50_out, h, x2);
  and and_11 (and_11_out, a, not_51_out, c, not_52_out, e, not_53_out, g, not_54_out, x2);
  and and_12 (and_12_out, a, not_55_out, c, d, e, not_56_out, g, h, x2);
  and and_13 (and_13_out, a, b, not_57_out, not_58_out, e, f, not_59_out, not_60_out, x2);
  and and_14 (and_14_out, a, b, not_61_out, d, e, f, not_62_out, h, x2);
  and and_15 (and_15_out, a, b, c, not_63_out, e, f, g, not_64_out, x2);
  and and_16 (and_16_out, a, b, c, d, e, f, g, h, x2);
  and and_17 (and_17_out, not_65_out, h, x2);
  and and_18 (and_18_out, not_66_out, g, x2);
  and and_19 (and_19_out, not_67_out, f, x2);
  and and_20 (and_20_out, not_68_out, e, x2);
  and and_21 (and_21_out, d, not_69_out, x2);
  and and_22 (and_22_out, c, not_70_out, x2);
  and and_23 (and_23_out, b, not_71_out, x2);
  and and_24 (and_24_out, a, not_72_out, x2);
  and and_25 (and_25_out, not_73_out, not_74_out, not_75_out, not_76_out, not_77_out, not_78_out, not_79_out, not_80_out, x2);
  and and_26 (and_26_out, not_81_out, not_82_out, not_83_out, d, not_84_out, not_85_out, not_86_out, h, x2);
  and and_27 (and_27_out, not_87_out, not_88_out, c, not_89_out, not_90_out, not_91_out, g, not_92_out, x2);
  and and_28 (and_28_out, not_93_out, not_94_out, c, d, not_95_out, not_96_out, g, h, x2);
  and and_29 (and_29_out, not_97_out, b, not_98_out, not_99_out, not_100_out, f, not_101_out, not_102_out, x2);
  and and_30 (and_30_out, not_103_out, b, not_104_out, d, not_105_out, f, not_106_out, h, x2);
  and and_31 (and_31_out, not_107_out, b, c, not_108_out, not_109_out, f, g, not_110_out, x2);
  and and_32 (and_32_out, not_111_out, b, c, d, not_112_out, f, g, h, x2);
  and and_33 (and_33_out, a, not_113_out, not_114_out, not_115_out, e, not_116_out, not_117_out, not_118_out, x2);
  and and_34 (and_34_out, a, not_119_out, not_120_out, d, e, not_121_out, not_122_out, h, x2);
  and and_35 (and_35_out, a, not_123_out, c, not_124_out, e, not_125_out, g, not_126_out, x2);
  and and_36 (and_36_out, a, not_127_out, c, d, e, not_128_out, g, h, x2);
  and and_37 (and_37_out, a, b, not_129_out, not_130_out, e, f, not_131_out, not_132_out, x2);
  and and_38 (and_38_out, a, b, not_133_out, d, e, f, not_134_out, h, x2);
  and and_39 (and_39_out, a, b, c, not_135_out, e, f, g, not_136_out, x2);
  and and_40 (and_40_out, a, b, c, d, e, f, g, h, x2);
  and and_41 (and_41_out, not_137_out, not_138_out, not_139_out, not_140_out, not_141_out, not_142_out, not_143_out, not_144_out, x2);
  and and_42 (and_42_out, not_145_out, not_146_out, not_147_out, d, not_148_out, not_149_out, not_150_out, h, x2);
  and and_43 (and_43_out, not_151_out, not_152_out, c, not_153_out, not_154_out, not_155_out, g, not_156_out, x2);
  and and_44 (and_44_out, not_157_out, not_158_out, c, d, not_159_out, not_160_out, g, h, x2);
  and and_45 (and_45_out, not_161_out, b, not_162_out, not_163_out, not_164_out, f, not_165_out, not_166_out, x2);
  and and_46 (and_46_out, not_167_out, b, not_168_out, d, not_169_out, f, not_170_out, h, x2);
  and and_47 (and_47_out, not_171_out, b, c, not_172_out, not_173_out, f, g, not_174_out, x2);
  and and_48 (and_48_out, not_175_out, b, c, d, not_176_out, f, g, h, x2);
  and and_49 (and_49_out, a, not_177_out, not_178_out, not_179_out, e, not_180_out, not_181_out, not_182_out, x2);
  and and_50 (and_50_out, a, not_183_out, not_184_out, d, e, not_185_out, not_186_out, h, x2);
  and and_51 (and_51_out, a, not_187_out, c, not_188_out, e, not_189_out, g, not_190_out, x2);
  and and_52 (and_52_out, a, not_191_out, c, d, e, not_192_out, g, h, x2);
  and and_53 (and_53_out, a, b, not_193_out, not_194_out, e, f, not_195_out, not_196_out, x2);
  and and_54 (and_54_out, a, b, not_197_out, d, e, f, not_198_out, h, x2);
  and and_55 (and_55_out, a, b, c, not_199_out, e, f, g, not_200_out, x2);
  and and_56 (and_56_out, a, b, c, d, e, f, g, h, x2);
  or or_1 (y, and_17_out, and_18_out, and_19_out, and_20_out, and_21_out, and_22_out, and_23_out, and_24_out);
  or or_2 (x, and_1_out, and_2_out, and_3_out, and_4_out, and_5_out, and_6_out, and_7_out, and_8_out, and_9_out, and_10_out, and_11_out, and_12_out, and_13_out, and_14_out, and_15_out, and_16_out);
  or or_3 (z, and_25_out, and_26_out, and_27_out, and_28_out, and_29_out, and_30_out, and_31_out, and_32_out, and_33_out, and_34_out, and_35_out, and_36_out, and_37_out, and_38_out, and_39_out, and_40_out);
  or or_4 (u, and_41_out, and_42_out, and_43_out, and_44_out, and_45_out, and_46_out, and_47_out, and_48_out, and_49_out, and_50_out, and_51_out, and_52_out, and_53_out, and_54_out, and_55_out, and_56_out);
endmodule
